# Fritzing sketch arduino_die_cathode (saved by Fritzing 0.8.7b)
breadboards: 1

parts:
  S1 = Pushbutton [package="[THT]"]
  Onderdeel1 = Arduino Nano (Rev3.0)
  7_Segment1 = 7 Segment Display
  R4 = Resistor [tolerance=±5% resistance=10k package=THT]
  R5 = Resistor [tolerance=±5% resistance=1k package=THT]

nets:
  N1: S1.Pin_1, S1.Pin_2, Onderdeel1.D2, R4.Pin_0
  N2: S1.Pin_3, S1.Pin_4, Onderdeel1.5V
  N3: Onderdeel1.GND, R4.Pin_1, R5.Pin_0
  N4: Onderdeel1.D4, 7_Segment1.Segment_DP
  N5: Onderdeel1.D5, 7_Segment1.Segment_G
  N6: Onderdeel1.D6, 7_Segment1.Segment_F
  N7: Onderdeel1.D7, 7_Segment1.Segment_E
  N8: Onderdeel1.D8, 7_Segment1.Segment_D
  N9: Onderdeel1.D9, 7_Segment1.Segment_C
  N10: Onderdeel1.D10, 7_Segment1.Segment_B
  N11: Onderdeel1.D11/MOSI, 7_Segment1.Segment_A
  N12: 7_Segment1.common_anode, R5.Pin_1

notes:
  1k ohm
  10k ohm
